// Logisim project Register.circ as structural Verilog: 1 circuit, main circuit main
module main (
  input  i1,
  input  in_2,
  input  in_3,
  input  in_4,
  input  Select,
  input  in_6
);

  wire and_1_out, and_2_out, and_3_out, and_4_out, and_5_out, and_6_out, and_7_out, and_8_out, and_9_out,
       and_10_out, and_11_out, and_12_out, not_1_out, not_2_out, not_3_out, not_4_out, not_5_out, not_6_out,
       not_7_out, not_8_out, not_9_out, not_10_out, not_11_out, not_12_out, or_1_out, or_2_out, or_3_out,
       or_4_out, or_5_out, or_6_out, or_7_out, or_8_out;

  and and_1 (and_1_out, Select, i1, in_6);
  and and_2 (and_2_out, Select, not_1_out, in_6);
  not not_1 (not_1_out, i1);
  or or_1 (or_1_out, and_1_out, not_3_out);
  or or_2 (or_2_out, not_2_out, and_2_out);
  LED led_1 (.in(and_3_out));
  not not_2 (not_2_out, or_1_out);
  not not_3 (not_3_out, or_2_out);
  and and_3 (and_3_out, Select, not_3_out);
  and and_4 (and_4_out, Select, in_2, in_6);
  not not_4 (not_4_out, in_2);
  or or_3 (or_3_out, and_4_out, not_6_out);
  or or_4 (or_4_out, not_5_out, and_5_out);
  and and_5 (and_5_out, Select, not_4_out, in_6);
  LED led_2 (.in(and_6_out));
  not not_5 (not_5_out, or_3_out);
  not not_6 (not_6_out, or_4_out);
  and and_6 (and_6_out, Select, not_6_out);
  LED led_3 (.in(and_9_out));
  and and_7 (and_7_out, Select, in_4, in_6);
  not not_7 (not_7_out, in_4);
  and and_8 (and_8_out, Select, not_7_out, in_6);
  or or_5 (or_5_out, and_7_out, not_9_out);
  or or_6 (or_6_out, not_8_out, and_8_out);
  not not_8 (not_8_out, or_5_out);
  not not_9 (not_9_out, or_6_out);
  and and_9 (and_9_out, Select, not_9_out);
  and and_10 (and_10_out, Select, in_3, in_6);
  and and_11 (and_11_out, Select, not_10_out, in_6);
  not not_10 (not_10_out, in_3);
  or or_7 (or_7_out, and_10_out, not_12_out);
  or or_8 (or_8_out, not_11_out, and_11_out);
  LED led_4 (.in(and_12_out));
  not not_11 (not_11_out, or_7_out);
  not not_12 (not_12_out, or_8_out);
  and and_12 (and_12_out, Select, not_12_out);

  // Notes on the sheet:
  //   set q = 1
  //   o1
  //   set q = 1
  //   o2
  //   set q = 1
  //   set q = 1
endmodule
