// Logisim project Volladdierer.circ as structural Verilog: 1 circuit, main circuit main
module main (
  input  in_1,
  input  in_2,
  input  in_3
);

  wire and_1_out, and_2_out, or_1_out, xor_1_out, xor_2_out;

  LED led_1 (.in(or_1_out));
  and and_1 (and_1_out, in_1, in_1);
  or or_1 (or_1_out, and_1_out, and_2_out);
  xor xor_1 (xor_1_out, in_1, in_1);
  and and_2 (and_2_out, xor_1_out, in_3);
  xor xor_2 (xor_2_out, xor_1_out, in_3);
  LED led_2 (.in(xor_2_out));

  assign in_2 = in_1;
endmodule
