// Logisim project addierer.circ as structural Verilog: 1 circuit, main circuit main
module main (
  input  in_1,
  input  in_2
);

  wire xor_2_out;

  // XOR_Gate xor_1 is placed but not wired
  // AND_Gate and_1 has open pins: in0=in_1, in1=in_1, out=open
  xor xor_2 (xor_2_out, in_1, in_1);
  LED led_1 (.in(xor_2_out));

  assign in_2 = in_1;
endmodule
