// Logisim project components.circ as structural Verilog
module Rs_Flipflop (
  input  reset,
  input  set,
  output q,
  output out_4
);

  wire or_1_out, or_2_out;

  or or_1 (or_1_out, reset, out_4);
  or or_2 (or_2_out, q, set);
  not not_1 (q, or_1_out);
  not not_2 (out_4, or_2_out);
endmodule

module Halbaddierer (
  input  B,
  input  A,
  output \Übertrag ,
  output Xor
);

  and and_1 (\Übertrag , B, A);
  xor xor_1 (Xor, B, A);
endmodule

module Volladdierer (
  input  in_1,
  input  in_2,
  input  in_3,
  output U,
  output Wert
);

  wire halbaddierer_1_xor, \halbaddierer_1_übertrag , \halbaddierer_2_übertrag ;

  xor xor_1 (U, \halbaddierer_1_übertrag , \halbaddierer_2_übertrag );
  Halbaddierer halbaddierer_1 (.\Übertrag (\halbaddierer_1_übertrag ), .B(in_1), .A(in_2), .Xor(halbaddierer_1_xor));
  Halbaddierer halbaddierer_2 (.\Übertrag (\halbaddierer_2_übertrag ), .B(halbaddierer_1_xor), .A(in_3), .Xor(Wert));
endmodule

module _4_Bit_Addierer (
  input  in_1,
  input  in_2,
  input  in_3,
  input  in_4,
  input  in_5,
  input  in_6,
  input  in_7,
  input  in_8,
  input  in_9,
  output out_10,
  output out_11,
  output out_12,
  output out_13,
  output out_14
);

  wire volladdierer_2_u, volladdierer_3_u, volladdierer_4_u;

  Volladdierer volladdierer_1 (.U(out_10), .in_3(volladdierer_2_u), .in_1(in_1), .in_2(in_2), .Wert(out_11));
  Volladdierer volladdierer_2 (.U(volladdierer_2_u), .in_3(volladdierer_3_u), .in_1(in_3), .in_2(in_4), .Wert(out_12));
  Volladdierer volladdierer_3 (.U(volladdierer_3_u), .in_3(volladdierer_4_u), .in_1(in_5), .in_2(in_6), .Wert(out_13));
  Volladdierer volladdierer_4 (.U(volladdierer_4_u), .in_3(in_9), .in_1(in_7), .in_2(in_8), .Wert(out_14));
endmodule

module Clock (
  output out_1
);

  wire clock_1_out, not_1_out, not_2_out, not_3_out, not_4_out;

  Clock_part clock_1 (.out(clock_1_out));
  not not_1 (not_1_out, clock_1_out);
  not not_2 (not_2_out, not_4_out);
  not not_3 (not_3_out, not_1_out);
  not not_4 (not_4_out, not_3_out);
  and and_1 (out_1, clock_1_out, not_2_out);
endmodule

module MemoryBlock (
  input  Select,
  input  Input,
  input  Write,
  output Ausgang
);

  wire and_1_out, and_2_out, not_1_out, rs_flipflop_1_q;

  and and_1 (and_1_out, Select, not_1_out, Write);
  not not_1 (not_1_out, Input);
  and and_2 (and_2_out, Select, Input, Write);
  Rs_Flipflop rs_flipflop_1 (.reset(and_1_out), .set(and_2_out), .q(rs_flipflop_1_q));  // open: out_4
  and and_3 (Ausgang, Select, rs_flipflop_1_q);
endmodule

// Addresse
module Register (
  input  a3,
  input  a2,
  input  a1,
  input  a0,
  input  Select,
  input  Write,
  output out_7,
  output out_8,
  output out_9,
  output out_10
);

  MemoryBlock memoryblock_1 (.Select(Select), .Input(a3), .Write(Write), .Ausgang(out_7));
  MemoryBlock memoryblock_2 (.Select(Select), .Input(a2), .Write(Write), .Ausgang(out_8));
  MemoryBlock memoryblock_3 (.Select(Select), .Input(a1), .Write(Write), .Ausgang(out_9));
  MemoryBlock memoryblock_4 (.Select(Select), .Input(a0), .Write(Write), .Ausgang(out_10));
endmodule

module _4_Bit_Binary_to_dec (
  input  i3,
  input  i2,
  input  i1,
  input  i0,
  output _15,
  output _14,
  output _13,
  output _12,
  output _11,
  output _10,
  output _9,
  output _8,
  output _7,
  output _6,
  output _5,
  output _4,
  output _3,
  output _2,
  output _1,
  output _0
);

  wire not_1_out, not_2_out, not_3_out, not_4_out;

  and and_1 (_14, i3, i2, i1, not_4_out);
  and and_2 (_15, i3, i2, i1, i0);
  not not_1 (not_1_out, i3);
  and and_3 (_13, not_3_out, i0, i2, i3);
  not not_2 (not_2_out, i2);
  and and_4 (_11, i3, not_2_out, i1, i0);
  and and_5 (_12, not_3_out, not_4_out, i3, i2);
  and and_6 (_10, not_2_out, not_4_out, i3, i1);
  not not_3 (not_3_out, i1);
  and and_7 (_8, not_2_out, not_3_out, not_4_out, i3);
  and and_8 (_9, not_2_out, not_3_out, i0, i3);
  and and_9 (_7, not_1_out, i2, i1, i0);
  and and_10 (_6, not_1_out, not_4_out, i2, i1);
  not not_4 (not_4_out, i0);
  and and_11 (_5, not_1_out, not_3_out, i2, i0);
  and and_12 (_3, not_1_out, not_2_out, i1, i0);
  and and_13 (_4, not_1_out, not_3_out, not_4_out, i2);
  and and_14 (_2, not_1_out, not_2_out, not_4_out, i1);
  and and_15 (_0, not_1_out, not_2_out, not_3_out, not_4_out);
  and and_16 (_1, not_1_out, not_2_out, not_3_out, i0);
endmodule

module _4_Bit_Add_and_Sub (
  input  b3,
  input  a3,
  input  b2,
  input  a2,
  input  b1,
  input  a1,
  input  b0,
  input  a0,
  input  SubOn,
  output out_10,
  output out_11,
  output out_12,
  output out_13,
  output out_14
);

  wire xor_1_out, xor_2_out, xor_3_out, xor_4_out;

  xor xor_1 (xor_1_out, b3, SubOn);
  xor xor_2 (xor_2_out, b2, SubOn);
  xor xor_3 (xor_3_out, b1, SubOn);
  xor xor_4 (xor_4_out, b0, SubOn);
  _4_Bit_Addierer u_4_bit_addierer_1 (
    .out_10(out_10), .in_9(SubOn), .in_1(xor_1_out), .in_2(a3), .in_3(xor_2_out), .in_4(a2),
    .in_5(xor_3_out), .in_6(a1), .in_7(xor_4_out), .in_8(a0), .out_11(out_11), .out_12(out_12),
    .out_13(out_13), .out_14(out_14));
endmodule

module Multiplier (
  input  in_1,
  input  Number_2,
  input  in_3,
  input  in_4,
  input  in_5,
  input  Number_1,
  input  in_7,
  input  in_8,
  output out_9,
  output out_10,
  output out_11,
  output out_12,
  output out_13,
  output out_14,
  output out_15,
  output out_16
);

  wire and_1_out, and_2_out, and_3_out, and_4_out, and_5_out, and_6_out, and_7_out, and_8_out, and_9_out,
       and_10_out, and_11_out, and_12_out, and_13_out, and_14_out, and_15_out, n4_bit_addierer_nd_2_out_10,
       n4_bit_addierer_nd_2_out_11, n4_bit_addierer_nd_2_out_12, n4_bit_addierer_nd_2_out_13,
       n4_bit_addierer_nd_3_out_10, n4_bit_addierer_nd_3_out_11, n4_bit_addierer_nd_3_out_12,
       n4_bit_addierer_nd_3_out_13;

  and and_1 (and_1_out, Number_2, in_5);
  and and_2 (and_2_out, in_1, in_5);
  and and_3 (and_3_out, in_3, in_5);
  and and_4 (and_4_out, in_4, in_5);
  and and_5 (and_5_out, in_1, Number_1);
  and and_6 (and_6_out, Number_2, Number_1);
  and and_7 (and_7_out, in_3, Number_1);
  and and_8 (and_8_out, in_4, Number_1);
  and and_9 (and_9_out, Number_2, in_7);
  and and_10 (and_10_out, in_1, in_7);
  _4_Bit_Addierer_ND u_4_bit_addierer_nd_1 (
    .out_10(out_13), .in_9(1'b0), .in_1(and_2_out), .in_2(and_1_out), .in_3(and_3_out), .in_4(and_4_out),
    .in_5(n4_bit_addierer_nd_2_out_10), .in_6(n4_bit_addierer_nd_2_out_11),
    .in_7(n4_bit_addierer_nd_2_out_12), .in_8(n4_bit_addierer_nd_2_out_13), .out_11(out_14), .out_12(out_15),
    .out_13(out_16), .out_14(out_9));
  and and_11 (and_11_out, in_3, in_7);
  and and_12 (and_12_out, in_4, in_7);
  and and_13 (and_13_out, in_1, in_8);
  _4_Bit_Addierer_ND u_4_bit_addierer_nd_2 (
    .out_10(n4_bit_addierer_nd_2_out_10), .in_9(1'b0), .in_1(and_5_out), .in_2(and_6_out), .in_3(and_7_out),
    .in_4(and_8_out), .in_5(n4_bit_addierer_nd_3_out_10), .in_6(n4_bit_addierer_nd_3_out_11),
    .in_7(n4_bit_addierer_nd_3_out_12), .in_8(n4_bit_addierer_nd_3_out_13),
    .out_11(n4_bit_addierer_nd_2_out_11), .out_12(n4_bit_addierer_nd_2_out_12),
    .out_13(n4_bit_addierer_nd_2_out_13), .out_14(out_10));
  and and_14 (and_14_out, Number_2, in_8);
  _4_Bit_Addierer_ND u_4_bit_addierer_nd_3 (
    .out_10(n4_bit_addierer_nd_3_out_10), .in_9(1'b0), .in_1(and_10_out), .in_2(and_9_out),
    .in_3(and_11_out), .in_4(and_12_out), .in_5(1'b0), .in_6(and_13_out), .in_7(and_14_out),
    .in_8(and_15_out), .out_11(n4_bit_addierer_nd_3_out_11), .out_12(n4_bit_addierer_nd_3_out_12),
    .out_13(n4_bit_addierer_nd_3_out_13), .out_14(out_11));
  and and_15 (and_15_out, in_3, in_8);
  and and_16 (out_12, in_4, in_8);

  // Notes on the sheet:
  //   Overflow
endmodule

module _8_Bit_Addierer (
  input  in_1,
  input  in_2,
  input  in_3,
  input  in_4,
  input  in_5,
  input  in_6,
  input  in_7,
  input  in_8,
  input  in_9,
  input  in_10,
  input  in_11,
  input  in_12,
  input  in_13,
  input  in_14,
  input  in_15,
  input  in_16,
  input  in_17,
  output out_18,
  output out_19,
  output out_20,
  output out_21,
  output out_22,
  output out_23,
  output out_24,
  output out_25,
  output out_26
);

  wire n4_bit_addierer_2_out_10;

  _4_Bit_Addierer u_4_bit_addierer_1 (
    .out_10(out_18), .in_9(n4_bit_addierer_2_out_10), .in_1(in_1), .in_2(in_2), .in_3(in_3), .in_4(in_4),
    .in_5(in_5), .in_6(in_6), .in_7(in_7), .in_8(in_8), .out_11(out_19), .out_12(out_20), .out_13(out_21),
    .out_14(out_22));
  _4_Bit_Addierer u_4_bit_addierer_2 (
    .out_10(n4_bit_addierer_2_out_10), .in_9(in_17), .in_1(in_9), .in_2(in_10), .in_3(in_11), .in_4(in_12),
    .in_5(in_13), .in_6(in_14), .in_7(in_15), .in_8(in_16), .out_11(out_23), .out_12(out_24),
    .out_13(out_25), .out_14(out_26));
endmodule

module _8_Bit_Adder_ND (
  input  in_1,
  input  in_2,
  input  in_3,
  input  in_4,
  input  in_5,
  input  in_6,
  input  in_7,
  input  in_8,
  input  in_9,
  input  in_10,
  input  in_11,
  input  in_12,
  input  in_13,
  input  in_14,
  input  in_15,
  input  in_16,
  input  in_17,
  output out_18,
  output out_19,
  output out_20,
  output out_21,
  output out_22,
  output out_23,
  output out_24,
  output out_25,
  output out_26
);

  _8_Bit_Addierer u_8_bit_addierer_1 (
    .out_18(out_18), .in_17(in_17), .in_1(in_1), .in_2(in_9), .in_3(in_2), .in_4(in_10), .in_5(in_3),
    .in_6(in_11), .in_7(in_4), .in_8(in_12), .in_9(in_5), .in_10(in_13), .in_11(in_6), .in_12(in_14),
    .in_13(in_7), .in_14(in_15), .in_15(in_8), .in_16(in_16), .out_19(out_19), .out_20(out_20),
    .out_21(out_21), .out_22(out_22), .out_23(out_23), .out_24(out_24), .out_25(out_25), .out_26(out_26));
endmodule

module _4_Bit_Addierer_ND (
  input  in_1,
  input  in_2,
  input  in_3,
  input  in_4,
  input  in_5,
  input  in_6,
  input  in_7,
  input  in_8,
  input  in_9,
  output out_10,
  output out_11,
  output out_12,
  output out_13,
  output out_14
);

  _4_Bit_Addierer u_4_bit_addierer_1 (
    .out_10(out_10), .in_9(in_9), .in_1(in_1), .in_2(in_5), .in_3(in_2), .in_4(in_6), .in_5(in_3),
    .in_6(in_7), .in_7(in_4), .in_8(in_8), .out_11(out_11), .out_12(out_12), .out_13(out_13), .out_14(out_14));
endmodule

module Divider (
  input  Divisor,
  input  in_2,
  input  in_3,
  input  in_4,
  input  in_5,
  input  Dividend,
  input  in_7,
  input  in_8,
  output out_9,
  output out_10,
  output out_11,
  output out_12,
  output out_13,
  output out_14,
  output out_15,
  output out_16
);

  wire get_mostleft_1_out_5, get_mostleft_1_out_6, get_mostleft_1_out_7, get_mostleft_1_out_8,
       n4_bit_add_and_sub_nd_1_out_12, n4_bit_add_and_sub_nd_1_out_13, n4_bit_add_and_sub_nd_1_out_14,
       n4_bit_add_and_sub_nd_2_out_12, n4_bit_add_and_sub_nd_2_out_13, n4_bit_add_and_sub_nd_2_out_14,
       n4_bit_add_and_sub_nd_3_out_12, n4_bit_add_and_sub_nd_3_out_13, n4_bit_add_and_sub_nd_3_out_14,
       n4_bit_add_and_sub_nd_4_out_11, n4_bit_add_and_sub_nd_4_out_12, n4_bit_add_and_sub_nd_4_out_13,
       n4_bit_add_and_sub_nd_4_out_14, n4_bit_multiplexer_1_out_10, n4_bit_multiplexer_1_out_11,
       n4_bit_multiplexer_1_out_12, n4_bit_multiplexer_1_out_13, n4_bit_multiplexer_2_out_10,
       n4_bit_multiplexer_2_out_11, n4_bit_multiplexer_2_out_12, n4_bit_multiplexer_2_out_13,
       n4_bit_multiplexer_3_out_10, n4_bit_multiplexer_3_out_11, n4_bit_multiplexer_3_out_12,
       n4_bit_multiplexer_3_out_13;

  _4_Bit_Multiplexer u_4_bit_multiplexer_1 (
    .in_9(out_9), .in_1(1'b0), .in_2(1'b0), .in_3(get_mostleft_1_out_8), .in_4(Dividend),
    .in_5(n4_bit_add_and_sub_nd_3_out_12), .in_6(n4_bit_add_and_sub_nd_3_out_13),
    .in_7(n4_bit_add_and_sub_nd_3_out_14), .in_8(Dividend), .out_10(n4_bit_multiplexer_1_out_10),
    .out_11(n4_bit_multiplexer_1_out_11), .out_12(n4_bit_multiplexer_1_out_12),
    .out_13(n4_bit_multiplexer_1_out_13));
  _4_Bit_Multiplexer u_4_bit_multiplexer_2 (
    .in_9(out_10), .in_1(n4_bit_multiplexer_1_out_11), .in_2(n4_bit_multiplexer_1_out_12),
    .in_3(n4_bit_multiplexer_1_out_13), .in_4(in_7), .in_5(n4_bit_add_and_sub_nd_1_out_12),
    .in_6(n4_bit_add_and_sub_nd_1_out_13), .in_7(n4_bit_add_and_sub_nd_1_out_14), .in_8(in_7),
    .out_10(n4_bit_multiplexer_2_out_10), .out_11(n4_bit_multiplexer_2_out_11),
    .out_12(n4_bit_multiplexer_2_out_12), .out_13(n4_bit_multiplexer_2_out_13));
  get_mostleft get_mostleft_1 (
    .in_1(in_5), .in_2(Dividend), .in_3(in_7), .in_4(in_8), .out_5(get_mostleft_1_out_5),
    .out_6(get_mostleft_1_out_6), .out_7(get_mostleft_1_out_7), .out_8(get_mostleft_1_out_8));
  _4_Bit_add_and_sub_ND u_4_bit_add_and_sub_nd_1 (
    .out_10(out_10), .in_9(1'b1), .in_1(Divisor), .in_2(in_2), .in_3(in_3), .in_4(in_4),
    .in_5(n4_bit_multiplexer_1_out_10), .in_6(n4_bit_multiplexer_1_out_11),
    .in_7(n4_bit_multiplexer_1_out_12), .in_8(n4_bit_multiplexer_1_out_13),
    .out_12(n4_bit_add_and_sub_nd_1_out_12), .out_13(n4_bit_add_and_sub_nd_1_out_13),
    .out_14(n4_bit_add_and_sub_nd_1_out_14));  // open: out_11
  _4_Bit_add_and_sub_ND u_4_bit_add_and_sub_nd_2 (
    .out_10(out_11), .in_9(1'b1), .in_1(Divisor), .in_2(in_2), .in_3(in_3), .in_4(in_4),
    .in_5(n4_bit_multiplexer_2_out_10), .in_6(n4_bit_multiplexer_2_out_11),
    .in_7(n4_bit_multiplexer_2_out_12), .in_8(n4_bit_multiplexer_2_out_13),
    .out_12(n4_bit_add_and_sub_nd_2_out_12), .out_13(n4_bit_add_and_sub_nd_2_out_13),
    .out_14(n4_bit_add_and_sub_nd_2_out_14));  // open: out_11
  _4_Bit_Multiplexer u_4_bit_multiplexer_3 (
    .in_9(out_11), .in_1(n4_bit_multiplexer_2_out_11), .in_2(n4_bit_multiplexer_2_out_12),
    .in_3(n4_bit_multiplexer_2_out_13), .in_4(in_8), .in_5(n4_bit_add_and_sub_nd_2_out_12),
    .in_6(n4_bit_add_and_sub_nd_2_out_13), .in_7(n4_bit_add_and_sub_nd_2_out_14), .in_8(in_8),
    .out_10(n4_bit_multiplexer_3_out_10), .out_11(n4_bit_multiplexer_3_out_11),
    .out_12(n4_bit_multiplexer_3_out_12), .out_13(n4_bit_multiplexer_3_out_13));
  _4_Bit_add_and_sub_ND u_4_bit_add_and_sub_nd_3 (
    .out_10(out_9), .in_9(1'b1), .in_1(Divisor), .in_2(in_2), .in_3(in_3), .in_4(in_4),
    .in_5(get_mostleft_1_out_5), .in_6(get_mostleft_1_out_6), .in_7(get_mostleft_1_out_7),
    .in_8(get_mostleft_1_out_8), .out_12(n4_bit_add_and_sub_nd_3_out_12),
    .out_13(n4_bit_add_and_sub_nd_3_out_13), .out_14(n4_bit_add_and_sub_nd_3_out_14));  // open: out_11
  _4_Bit_add_and_sub_ND u_4_bit_add_and_sub_nd_4 (
    .out_10(out_12), .in_9(1'b1), .in_1(Divisor), .in_2(in_2), .in_3(in_3), .in_4(in_4),
    .in_5(n4_bit_multiplexer_3_out_10), .in_6(n4_bit_multiplexer_3_out_11),
    .in_7(n4_bit_multiplexer_3_out_12), .in_8(n4_bit_multiplexer_3_out_13),
    .out_11(n4_bit_add_and_sub_nd_4_out_11), .out_12(n4_bit_add_and_sub_nd_4_out_12),
    .out_13(n4_bit_add_and_sub_nd_4_out_13), .out_14(n4_bit_add_and_sub_nd_4_out_14));
  _4_Bit_Multiplexer u_4_bit_multiplexer_4 (
    .in_9(out_12), .in_1(n4_bit_multiplexer_3_out_10), .in_2(n4_bit_multiplexer_3_out_11),
    .in_3(n4_bit_multiplexer_3_out_12), .in_4(n4_bit_multiplexer_3_out_13),
    .in_5(n4_bit_add_and_sub_nd_4_out_11), .in_6(n4_bit_add_and_sub_nd_4_out_12),
    .in_7(n4_bit_add_and_sub_nd_4_out_13), .in_8(n4_bit_add_and_sub_nd_4_out_14), .out_10(out_13),
    .out_11(out_14), .out_12(out_15), .out_13(out_16));
endmodule

module _4_Bit_add_and_sub_ND (
  input  in_1,
  input  in_2,
  input  in_3,
  input  in_4,
  input  in_5,
  input  in_6,
  input  in_7,
  input  in_8,
  input  in_9,
  output out_10,
  output out_11,
  output out_12,
  output out_13,
  output out_14
);

  _4_Bit_Add_and_Sub u_4_bit_add_and_sub_1 (
    .out_10(out_10), .SubOn(in_9), .b3(in_1), .a3(in_5), .b2(in_2), .a2(in_6), .b1(in_3), .a1(in_7),
    .b0(in_4), .a0(in_8), .out_11(out_11), .out_12(out_12), .out_13(out_13), .out_14(out_14));
endmodule

module get_mostleft (
  input  in_1,
  input  in_2,
  input  in_3,
  input  in_4,
  output out_5,
  output out_6,
  output out_7,
  output out_8
);


  assign out_5 = 1'b0;
  assign out_6 = 1'b0;
  assign out_7 = 1'b0;
  assign out_8 = in_1;
endmodule

module Multiplexer (
  input  in_1,
  input  in_2,
  input  in_3,
  output out_4
);

  wire and_1_out, and_2_out, not_1_out;

  not not_1 (not_1_out, in_2);
  and and_1 (and_1_out, in_1, in_2);
  and and_2 (and_2_out, not_1_out, in_3);
  or or_1 (out_4, and_1_out, and_2_out);
endmodule

module _4_Bit_Multiplexer (
  input  in_1,
  input  in_2,
  input  in_3,
  input  in_4,
  input  in_5,
  input  in_6,
  input  in_7,
  input  in_8,
  input  in_9,
  output out_10,
  output out_11,
  output out_12,
  output out_13
);

  Multiplexer multiplexer_1 (.in_1(in_5), .in_2(in_9), .in_3(in_1), .out_4(out_10));
  Multiplexer multiplexer_2 (.in_1(in_6), .in_2(in_9), .in_3(in_2), .out_4(out_11));
  Multiplexer multiplexer_3 (.in_1(in_7), .in_2(in_9), .in_3(in_3), .out_4(out_12));
  Multiplexer multiplexer_4 (.in_1(in_8), .in_2(in_9), .in_3(in_4), .out_4(out_13));
endmodule

module and_and_or (
  input  A,
  input  B,
  output out_3,
  output out_4
);

  or or_1 (out_3, A, B);
  and and_1 (out_4, A, B);
endmodule

module _1_Bit_ALU (
  input  A,
  input  B,
  input  A_Inverter,
  input  B_Inverter,
  input  Cin,
  input  Summe,
  input  Or,
  input  And,
  output Cout,
  output Ausgabe
);

  wire and_and_or_1_out_3, and_and_or_1_out_4, volladdierer_1_wert, xor_1_out, xor_2_out;

  xor xor_1 (xor_1_out, A, A_Inverter);
  Volladdierer volladdierer_1 (.U(Cout), .in_3(Cin), .in_1(xor_1_out), .in_2(xor_2_out), .Wert(volladdierer_1_wert));
  assign Ausgabe = Summe ? volladdierer_1_wert : 1'bz;  // Controlled_Buffer controlled_buffer_1
  xor xor_2 (xor_2_out, B, B_Inverter);
  and_and_or and_and_or_1 (.A(xor_1_out), .B(xor_2_out), .out_3(and_and_or_1_out_3), .out_4(and_and_or_1_out_4));
  assign Ausgabe = Or ? and_and_or_1_out_3 : 1'bz;  // Controlled_Buffer controlled_buffer_2
  assign Ausgabe = And ? and_and_or_1_out_4 : 1'bz;  // Controlled_Buffer controlled_buffer_3
endmodule

module _4_Bit_ALU (
  input  in_1,
  input  in_2,
  input  in_3,
  input  in_4,
  input  in_5,
  input  in_6,
  input  in_7,
  input  in_8,
  input  in_9,
  input  in_10,
  input  in_11,
  input  in_12,
  input  in_13,
  input  in_14,
  output out_15,
  output out_16,
  output out_17,
  output out_18,
  output out_19,
  output Carry,
  output Zero,
  output Negative,
  output Overflow
);

  wire n1_bit_alu_2_cout, n1_bit_alu_3_cout, n1_bit_alu_4_cout;

  nor nor_1 (Zero, Negative, out_17, out_18, out_19);
  xor xor_1 (Overflow, Carry, n1_bit_alu_2_cout);
  _1_Bit_ALU u_1_bit_alu_1 (
    .Cout(Carry), .A_Inverter(in_9), .B_Inverter(in_10), .Cin(n1_bit_alu_2_cout), .Summe(in_12), .Or(in_13),
    .And(in_14), .A(in_1), .B(in_5), .Ausgabe(Negative));
  _1_Bit_ALU u_1_bit_alu_2 (
    .Cout(n1_bit_alu_2_cout), .A_Inverter(in_9), .B_Inverter(in_10), .Cin(n1_bit_alu_3_cout), .Summe(in_12),
    .Or(in_13), .And(in_14), .A(in_2), .B(in_6), .Ausgabe(out_17));
  _1_Bit_ALU u_1_bit_alu_3 (
    .Cout(n1_bit_alu_3_cout), .A_Inverter(in_9), .B_Inverter(in_10), .Cin(n1_bit_alu_4_cout), .Summe(in_12),
    .Or(in_13), .And(in_14), .A(in_3), .B(in_7), .Ausgabe(out_18));
  _1_Bit_ALU u_1_bit_alu_4 (
    .Cout(n1_bit_alu_4_cout), .A_Inverter(in_9), .B_Inverter(in_10), .Cin(in_11), .Summe(in_12), .Or(in_13),
    .And(in_14), .A(in_4), .B(in_8), .Ausgabe(out_19));

  assign out_15 = Carry;
  assign out_16 = Negative;

  // Notes on the sheet:
  //   A
  //   B
endmodule

module Counter_4_Bit (
  input  in_1,
  output out_2,
  output out_3,
  output out_4,
  output out_5
);

  wire clock_1_out, n4_bit_addierer_nd_1_out_11, n4_bit_addierer_nd_1_out_12, n4_bit_addierer_nd_1_out_13,
       n4_bit_addierer_nd_1_out_14;

  Clock_part clock_1 (.out(clock_1_out));
  _4_Bit_Addierer_ND u_4_bit_addierer_nd_1 (
    .in_9(1'b0), .in_1(1'b0), .in_2(1'b0), .in_3(1'b0), .in_4(1'b1), .in_5(out_2), .in_6(out_3),
    .in_7(out_4), .in_8(out_5), .out_11(n4_bit_addierer_nd_1_out_11), .out_12(n4_bit_addierer_nd_1_out_12),
    .out_13(n4_bit_addierer_nd_1_out_13), .out_14(n4_bit_addierer_nd_1_out_14));  // open: out_10
  Register register_1 (
    .Select(clock_1_out), .Write(in_1), .a3(n4_bit_addierer_nd_1_out_11), .a2(n4_bit_addierer_nd_1_out_12),
    .a1(n4_bit_addierer_nd_1_out_13), .a0(n4_bit_addierer_nd_1_out_14), .out_7(out_2), .out_8(out_3),
    .out_9(out_4), .out_10(out_5));
endmodule

module _8_Bit_Alu (
  input  in_1,
  input  in_2,
  input  in_3,
  input  in_4,
  input  in_5,
  input  in_6,
  input  in_7,
  input  in_8,
  input  in_9,
  input  in_10,
  input  in_11,
  input  in_12,
  input  in_13,
  input  in_14,
  input  in_15,
  input  in_16,
  input  in_17,
  input  in_18,
  input  in_19,
  input  in_20,
  input  in_21,
  input  in_22,
  output Cout,
  output Carry,
  output Negative,
  output Overflow,
  output Zero,
  output out_28,
  output out_29,
  output out_30,
  output out_31,
  output out_32,
  output out_33,
  output out_34,
  output out_35
);

  wire n4_bit_alu_1_zero, n4_bit_alu_2_out_15, n4_bit_alu_2_zero;

  and and_1 (Zero, n4_bit_alu_1_zero, n4_bit_alu_2_zero);
  _4_Bit_ALU u_4_bit_alu_1 (
    .in_1(in_1), .in_2(in_2), .in_3(in_3), .in_4(in_4), .in_5(in_9), .in_6(in_10), .in_7(in_11),
    .in_8(in_12), .out_15(Cout), .in_9(in_18), .in_10(in_19), .in_11(n4_bit_alu_2_out_15), .in_12(in_20),
    .in_13(in_21), .in_14(in_22), .out_16(out_28), .out_17(out_29), .out_18(out_30), .out_19(out_31),
    .Carry(Carry), .Zero(n4_bit_alu_1_zero), .Negative(Negative), .Overflow(Overflow));
  _4_Bit_ALU u_4_bit_alu_2 (
    .in_1(in_5), .in_2(in_6), .in_3(in_7), .in_4(in_8), .in_5(in_13), .in_6(in_14), .in_7(in_15),
    .in_8(in_16), .out_15(n4_bit_alu_2_out_15), .in_9(in_18), .in_10(in_19), .in_11(in_17), .in_12(in_20),
    .in_13(in_21), .in_14(in_22), .out_16(out_32), .out_17(out_33), .out_18(out_34), .out_19(out_35),
    .Zero(n4_bit_alu_2_zero));  // open: Carry, Negative, Overflow
endmodule

module _8_Bit_Register (
  input  in_1,
  input  in_2,
  input  in_3,
  input  in_4,
  input  in_5,
  input  in_6,
  input  in_7,
  input  in_8,
  input  in_9,
  input  in_10,
  output out_11,
  output out_12,
  output out_13,
  output out_14,
  output out_15,
  output out_16,
  output out_17,
  output out_18
);

  Register register_1 (
    .Select(in_9), .Write(in_10), .a3(in_1), .a2(in_2), .a1(in_3), .a0(in_4), .out_7(out_11), .out_8(out_12),
    .out_9(out_13), .out_10(out_14));
  Register register_2 (
    .Select(in_9), .Write(in_10), .a3(in_5), .a2(in_6), .a1(in_7), .a0(in_8), .out_7(out_15), .out_8(out_16),
    .out_9(out_17), .out_10(out_18));
endmodule

module _8_Bit_Steuerwerk (
  input  in_1,
  input  in_2,
  input  in_3,
  input  Reset
);

  wire and_1_out, and_2_out, and_3_out, and_4_out, and_5_out, and_6_out, and_8_out, and_9_out, and_10_out,
       and_11_out, and_12_out, and_13_out, and_14_out, and_15_out, and_16_out, and_17_out, and_18_out,
       Buffer_Pahse_out, clock_1_out, is_ax_1_out_9, is_bx_1_out_9, multiplexer_1_out, n8_bit_decoder_1_add,
       n8_bit_decoder_1_and, n8_bit_decoder_1_hlt, n8_bit_decoder_1_ld, n8_bit_decoder_1_mov,
       n8_bit_decoder_1_or, n8_bit_decoder_1_sub, nand_1_out, nor_1_out, nor_2_out, nor_3_out, nor_4_out,
       nor_5_out, nor_6_out, nor_7_out, nor_8_out, not_1_out, not_2_out, not_3_out, not_4_out, not_5_out,
       not_6_out, not_7_out, not_8_out, not_9_out, not_10_out, not_11_out, not_12_out, not_13_out,
       not_14_out, or_1_out, or_2_out;
  wire [7:0] AX_out_19, Buffer_out_19, BX_out_19, counter_1_q, Cycle_q, Ergebnis_out_19,
       index_register_1_out_5, Instruction_Register_out_19, n8_bit_alu_1_out_35, Op1_out_19, ram_1_data;

  or or_1 (or_1_out, clock_1_out, Reset);
  Clock_part clock_1 (.out(clock_1_out));
  LED led_1 (.in(Cycle_q[7]));
  Counter_part #(.max('h8)) counter_1 (.Q(counter_1_q), .clk(clock_1_out), .clr(Reset));  // open: load, D, count, carry
  Counter_part Cycle (.Q(Cycle_q), .clk(and_2_out), .clr(Reset));  // open: load, D, count, carry
  LED led_2 (.in(Cycle_q[3]));
  LED led_3 (.in(Cycle_q[6]));
  LED led_4 (.in(Cycle_q[5]));
  LED led_5 (.in(Cycle_q[4]));
  not not_1 (not_1_out, counter_1_q[0]);
  not not_2 (not_2_out, counter_1_q[1]);
  not not_3 (not_3_out, counter_1_q[0]);
  not not_4 (not_4_out, counter_1_q[1]);
  LED led_6 (.in(Cycle_q[2]));
  LED led_7 (.in(Cycle_q[0]));
  LED led_8 (.in(Cycle_q[1]));
  nor Buffer_Pahse (Buffer_Pahse_out, counter_1_q[0], counter_1_q[1], counter_1_q[2], counter_1_q[3]);
  nor nor_1 (nor_1_out, not_1_out, counter_1_q[1], counter_1_q[2], counter_1_q[3]);
  nor nor_2 (nor_2_out, counter_1_q[0], not_2_out, counter_1_q[2], counter_1_q[3]);
  nor nor_3 (nor_3_out, not_3_out, not_4_out, counter_1_q[2], counter_1_q[3]);
  nor nor_4 (nor_4_out, counter_1_q[0], counter_1_q[1], not_5_out, counter_1_q[3]);
  not not_5 (not_5_out, counter_1_q[2]);
  not not_6 (not_6_out, counter_1_q[0]);
  nor nor_5 (nor_5_out, not_6_out, counter_1_q[1], not_7_out, counter_1_q[3]);
  not not_7 (not_7_out, counter_1_q[2]);
  not not_8 (not_8_out, counter_1_q[1]);
  nor nor_6 (nor_6_out, counter_1_q[0], not_8_out, not_9_out, counter_1_q[3]);
  not not_9 (not_9_out, counter_1_q[2]);
  not not_10 (not_10_out, counter_1_q[0]);
  not not_11 (not_11_out, counter_1_q[1]);
  nor nor_7 (nor_7_out, not_10_out, not_11_out, not_12_out, counter_1_q[3]);
  not not_12 (not_12_out, counter_1_q[2]);
  nor nor_8 (nor_8_out, counter_1_q[0], counter_1_q[1], counter_1_q[2], not_13_out);
  not not_13 (not_13_out, counter_1_q[3]);
  and and_1 (and_1_out, nand_1_out, not_14_out);
  not not_14 (not_14_out, 1'b0);
  and and_2 (and_2_out, Buffer_Pahse_out, and_1_out);
  and and_3 (and_3_out, nor_1_out, and_1_out);
  and and_4 (and_4_out, nor_2_out, and_1_out);
  and and_5 (and_5_out, nor_3_out, and_1_out);
  and and_6 (and_6_out, nor_4_out, and_1_out);
  // AND_Gate and_7 has open pins: in0=nor_5_out, in1=and_1_out, out=open
  and and_8 (and_8_out, nor_6_out, and_1_out);
  and and_9 (and_9_out, nor_7_out, and_1_out);
  and and_10 (and_10_out, nor_8_out, and_1_out);
  nand nand_1 (nand_1_out, index_register_1_out_5[0], index_register_1_out_5[1], index_register_1_out_5[2], index_register_1_out_5[3], index_register_1_out_5[4], index_register_1_out_5[5], index_register_1_out_5[6], index_register_1_out_5[6]);
  or or_2 (or_2_out, and_4_out, and_6_out);
  LED led_9 (.in(index_register_1_out_5[5]));
  LED led_10 (.in(index_register_1_out_5[6]));
  LED led_11 (.in(index_register_1_out_5[7]));
  Index_Register index_register_1 (
    .Increase(or_2_out), .Reset(Reset), .Read(1'b1), .clock(1'b1), .out_5(index_register_1_out_5));
  LED led_12 (.in(index_register_1_out_5[3]));
  LED led_13 (.in(index_register_1_out_5[4]));
  LED led_14 (.in(index_register_1_out_5[1]));
  LED led_15 (.in(index_register_1_out_5[2]));
  LED led_16 (.in(index_register_1_out_5[0]));
  // OR_Gate or_3 has open pins: in0=1'b1, out=open
  LED led_17 (.in(Instruction_Register_out_19[7]));
  LED led_18 (.in(Instruction_Register_out_19[6]));
  LED led_19 (.in(Instruction_Register_out_19[4]));
  LED led_20 (.in(Instruction_Register_out_19[5]));
  _8_Bit_Register_Clock Instruction_Register (
    .in_9(1'b1), .in_10(or_1_out), .in_11(and_3_out), .in_1(ram_1_data[7]), .in_2(ram_1_data[6]),
    .in_3(ram_1_data[5]), .in_4(ram_1_data[4]), .in_5(ram_1_data[3]), .in_6(ram_1_data[2]),
    .in_7(ram_1_data[1]), .in_8(ram_1_data[0]), .out_12(Instruction_Register_out_19[7]),
    .out_13(Instruction_Register_out_19[6]), .out_14(Instruction_Register_out_19[5]),
    .out_15(Instruction_Register_out_19[4]), .out_16(Instruction_Register_out_19[3]),
    .out_17(Instruction_Register_out_19[2]), .out_18(Instruction_Register_out_19[1]),
    .out_19(Instruction_Register_out_19[0]));
  LED led_21 (.in(Instruction_Register_out_19[1]));
  LED led_22 (.in(Instruction_Register_out_19[2]));
  LED led_23 (.in(Instruction_Register_out_19[3]));
  LED led_24 (.in(Instruction_Register_out_19[0]));
  LED led_25 (.in(Op1_out_19[7]));
  LED led_26 (.in(Op1_out_19[5]));
  LED led_27 (.in(Op1_out_19[6]));
  LED led_28 (.in(Op1_out_19[3]));
  LED led_29 (.in(Op1_out_19[4]));
  RAM ram_1 (.addr(index_register_1_out_5), .data(ram_1_data), .clk(1'b1));  // open: sel, ld, clr
  _8_Bit_Register_Clock Op1 (
    .in_9(1'b1), .in_10(or_1_out), .in_11(and_5_out), .in_1(ram_1_data[7]), .in_2(ram_1_data[6]),
    .in_3(ram_1_data[5]), .in_4(ram_1_data[4]), .in_5(ram_1_data[3]), .in_6(ram_1_data[2]),
    .in_7(ram_1_data[1]), .in_8(ram_1_data[0]), .out_12(Op1_out_19[7]), .out_13(Op1_out_19[6]),
    .out_14(Op1_out_19[5]), .out_15(Op1_out_19[4]), .out_16(Op1_out_19[3]), .out_17(Op1_out_19[2]),
    .out_18(Op1_out_19[1]), .out_19(Op1_out_19[0]));
  LED led_30 (.in(Op1_out_19[0]));
  LED led_31 (.in(Op1_out_19[2]));
  LED led_32 (.in(Op1_out_19[1]));
  is_ax is_ax_1 (
    .in_1(Op1_out_19[7]), .in_2(Op1_out_19[6]), .in_3(Op1_out_19[5]), .in_4(Op1_out_19[4]),
    .in_5(Op1_out_19[3]), .in_6(Op1_out_19[2]), .in_7(Op1_out_19[1]), .in_8(Op1_out_19[0]),
    .out_9(is_ax_1_out_9));
  _8_Bit_Decoder u_8_bit_decoder_1 (
    .SUB(n8_bit_decoder_1_sub), .ADD(n8_bit_decoder_1_add), .OR(n8_bit_decoder_1_or),
    .AND(n8_bit_decoder_1_and), .MOV(n8_bit_decoder_1_mov), .LD(n8_bit_decoder_1_ld),
    .HLT(n8_bit_decoder_1_hlt), .in_1(Instruction_Register_out_19[7]), .in_2(Instruction_Register_out_19[6]),
    .in_3(Instruction_Register_out_19[5]), .in_4(Instruction_Register_out_19[4]),
    .in_5(Instruction_Register_out_19[3]), .in_6(Instruction_Register_out_19[2]),
    .in_7(Instruction_Register_out_19[1]), .in_8(Instruction_Register_out_19[0]));
  LED led_33 (.in(AX_out_19[6]));
  LED led_34 (.in(AX_out_19[7]));
  LED led_35 (.in(AX_out_19[5]));
  _8_Bit_Register_Clock AX (
    .in_9(1'b1), .in_10(or_1_out), .in_11(and_11_out), .in_1(Ergebnis_out_19[7]), .in_2(Ergebnis_out_19[6]),
    .in_3(Ergebnis_out_19[5]), .in_4(Ergebnis_out_19[4]), .in_5(Ergebnis_out_19[3]),
    .in_6(Ergebnis_out_19[2]), .in_7(Ergebnis_out_19[1]), .in_8(Ergebnis_out_19[0]), .out_12(AX_out_19[7]),
    .out_13(AX_out_19[6]), .out_14(AX_out_19[5]), .out_15(AX_out_19[4]), .out_16(AX_out_19[3]),
    .out_17(AX_out_19[2]), .out_18(AX_out_19[1]), .out_19(AX_out_19[0]));
  and and_11 (and_11_out, is_ax_1_out_9, n8_bit_decoder_1_mov, and_10_out);
  LED led_36 (.in(AX_out_19[3]));
  LED led_37 (.in(AX_out_19[4]));
  LED led_38 (.in(AX_out_19[1]));
  LED led_39 (.in(AX_out_19[2]));
  LED led_40 (.in(BX_out_19[6]));
  LED led_41 (.in(AX_out_19[0]));
  LED led_42 (.in(BX_out_19[7]));
  and and_12 (and_12_out, is_bx_1_out_9, and_10_out, n8_bit_decoder_1_mov);
  is_bx is_bx_1 (
    .out_9(is_bx_1_out_9), .in_1(Op1_out_19[7]), .in_2(Op1_out_19[6]), .in_3(Op1_out_19[5]),
    .in_4(Op1_out_19[4]), .in_5(Op1_out_19[3]), .in_6(Op1_out_19[2]), .in_7(Op1_out_19[1]),
    .in_8(Op1_out_19[0]));
  LED led_43 (.in(BX_out_19[5]));
  LED led_44 (.in(BX_out_19[4]));
  LED led_45 (.in(BX_out_19[2]));
  LED led_46 (.in(BX_out_19[3]));
  and and_13 (and_13_out, and_9_out, n8_bit_decoder_1_sub);
  and and_14 (and_14_out, and_9_out, n8_bit_decoder_1_add);
  and and_15 (and_15_out, and_9_out, n8_bit_decoder_1_or);
  and and_16 (and_16_out, and_9_out, n8_bit_decoder_1_and);
  and and_17 (and_17_out, and_9_out, n8_bit_decoder_1_mov);
  and and_18 (and_18_out, and_9_out, n8_bit_decoder_1_ld);
  _8_Bit_Register_Clock Ergebnis (
    .in_9(1'b1), .in_10(or_1_out), .in_11(and_10_out), .in_1(Buffer_out_19[7]), .in_2(Buffer_out_19[6]),
    .in_3(Buffer_out_19[5]), .in_4(Buffer_out_19[4]), .in_5(Buffer_out_19[3]), .in_6(Buffer_out_19[2]),
    .in_7(Buffer_out_19[1]), .in_8(Buffer_out_19[0]), .out_12(Ergebnis_out_19[7]),
    .out_13(Ergebnis_out_19[6]), .out_14(Ergebnis_out_19[5]), .out_15(Ergebnis_out_19[4]),
    .out_16(Ergebnis_out_19[3]), .out_17(Ergebnis_out_19[2]), .out_18(Ergebnis_out_19[1]),
    .out_19(Ergebnis_out_19[0]));
  _8_Bit_Register_Clock BX (
    .in_9(1'b1), .in_10(or_1_out), .in_11(and_12_out), .in_1(Ergebnis_out_19[7]), .in_2(Ergebnis_out_19[6]),
    .in_3(Ergebnis_out_19[5]), .in_4(Ergebnis_out_19[4]), .in_5(Ergebnis_out_19[3]),
    .in_6(Ergebnis_out_19[2]), .in_7(Ergebnis_out_19[1]), .in_8(Ergebnis_out_19[0]), .out_12(BX_out_19[7]),
    .out_13(BX_out_19[6]), .out_14(BX_out_19[5]), .out_15(BX_out_19[4]), .out_16(BX_out_19[3]),
    .out_17(BX_out_19[2]), .out_18(BX_out_19[1]), .out_19(BX_out_19[0]));
  LED led_47 (.in(BX_out_19[0]));
  LED led_48 (.in(BX_out_19[1]));
  _8_Bit_Register_Clock Buffer (
    .in_10(or_1_out), .in_1(n8_bit_alu_1_out_35[7]), .in_2(n8_bit_alu_1_out_35[6]),
    .in_3(n8_bit_alu_1_out_35[5]), .in_4(n8_bit_alu_1_out_35[4]), .in_5(n8_bit_alu_1_out_35[3]),
    .in_6(n8_bit_alu_1_out_35[2]), .in_7(n8_bit_alu_1_out_35[1]), .in_8(n8_bit_alu_1_out_35[0]),
    .out_12(Buffer_out_19[7]), .out_13(Buffer_out_19[6]), .out_14(Buffer_out_19[5]),
    .out_15(Buffer_out_19[4]), .out_16(Buffer_out_19[3]), .out_17(Buffer_out_19[2]),
    .out_18(Buffer_out_19[1]), .out_19(Buffer_out_19[0]));  // open: in_9, in_11
  Multiplexer_part multiplexer_1 (.in0(in_1), .in1(in_2), .out(multiplexer_1_out), .sel(in_3), .en(or_1_out));
  _8_Bit_Alu u_8_bit_alu_1 (
    .in_1(Ergebnis_out_19[7]), .in_2(Ergebnis_out_19[6]), .in_3(Ergebnis_out_19[5]),
    .in_4(Ergebnis_out_19[4]), .in_5(Ergebnis_out_19[3]), .in_6(Ergebnis_out_19[2]),
    .in_7(Ergebnis_out_19[1]), .in_8(Ergebnis_out_19[0]), .out_28(n8_bit_alu_1_out_35[7]),
    .out_29(n8_bit_alu_1_out_35[6]), .out_30(n8_bit_alu_1_out_35[5]), .out_31(n8_bit_alu_1_out_35[4]),
    .out_32(n8_bit_alu_1_out_35[3]), .out_33(n8_bit_alu_1_out_35[2]), .out_34(n8_bit_alu_1_out_35[1]),
    .out_35(n8_bit_alu_1_out_35[0]));  // open: Cout, Carry, Negative, Overflow, Zero, in_17, in_18, in_19, in_20, in_21, in_22, in_9, in_10, in_11, in_12, in_13, in_14, in_15, in_16

  // Notes on the sheet:
  //   Cycle
  //   Increase
  //   Increase
  //   Fetch Instruction
  //   Fetch op1
  //   Render Phase
  //   Increase and decode
  //   Execute
  //   Write Back
  //   HLT Signal
  //   RAM
  //   is_ax
  //   is_bx
  //   AX
  //   BX
endmodule

module Counter (
  input  in_1,
  input  in_2,
  input  in_3
);

  wire undriven;

  Counter_part #(.width(2), .max('h3)) counter_1 (
    .load(in_1), .count(undriven), .clk(in_2), .clr(in_3));  // open: D, Q, carry
endmodule

module RS_Flipflop_clock (
  input  in_1,
  input  in_2,
  input  in_3,
  output out_4,
  output out_5
);

  wire and_1_out, and_2_out;

  and and_1 (and_1_out, in_1, in_2);
  and and_2 (and_2_out, in_2, in_3);
  Rs_Flipflop rs_flipflop_1 (.reset(and_1_out), .set(and_2_out), .q(out_4), .out_4(out_5));
endmodule

module _8_Bit_Register_Clock (
  input  in_1,
  input  in_2,
  input  in_3,
  input  in_4,
  input  in_5,
  input  in_6,
  input  in_7,
  input  in_8,
  input  in_9,
  input  in_10,
  input  in_11,
  output out_12,
  output out_13,
  output out_14,
  output out_15,
  output out_16,
  output out_17,
  output out_18,
  output out_19
);

  wire and_1_out, and_2_out;

  and and_1 (and_1_out, in_9, in_10);
  and and_2 (and_2_out, in_10, in_11);
  _8_Bit_Register u_8_bit_register_1 (
    .in_9(and_1_out), .in_10(and_2_out), .in_1(in_1), .in_2(in_2), .in_3(in_3), .in_4(in_4), .in_5(in_5),
    .in_6(in_6), .in_7(in_7), .in_8(in_8), .out_11(out_12), .out_12(out_13), .out_13(out_14),
    .out_14(out_15), .out_15(out_16), .out_16(out_17), .out_17(out_18), .out_18(out_19));
endmodule

module _8_Bit_Adder (
  input  in_1,
  input  in_2,
  input  in_3,
  input  in_4,
  input  in_5,
  input  in_6,
  input  in_7,
  input  in_8,
  input  in_9,
  input  in_10,
  input  in_11,
  input  in_12,
  input  in_13,
  input  in_14,
  input  in_15,
  input  in_16
);
endmodule

module \íncrease_counter  (
  input  [7:0] Wert,
  input  Select,
  output Cout
);

  wire clock_1_out, n8_bit_adder_nd_1_out_19, n8_bit_adder_nd_1_out_20, n8_bit_adder_nd_1_out_21,
       n8_bit_adder_nd_1_out_22, n8_bit_adder_nd_1_out_23, n8_bit_adder_nd_1_out_24,
       n8_bit_adder_nd_1_out_25, n8_bit_adder_nd_1_out_26, n8_bit_register_clock_1_out_12,
       n8_bit_register_clock_1_out_13, n8_bit_register_clock_1_out_14, n8_bit_register_clock_1_out_15,
       n8_bit_register_clock_1_out_16, n8_bit_register_clock_1_out_17, n8_bit_register_clock_1_out_18,
       n8_bit_register_clock_1_out_19, not_1_out, or_1_out;

  Clock_part clock_1 (.out(clock_1_out));
  not not_1 (not_1_out, clock_1_out);
  or or_1 (or_1_out, clock_1_out, not_1_out);
  _8_Bit_Register_Clock Puffer (
    .in_9(or_1_out), .in_10(or_1_out), .in_11(not_1_out), .in_1(n8_bit_adder_nd_1_out_19),
    .in_2(n8_bit_adder_nd_1_out_20), .in_3(n8_bit_adder_nd_1_out_21), .in_4(n8_bit_adder_nd_1_out_22),
    .in_5(n8_bit_adder_nd_1_out_23), .in_6(n8_bit_adder_nd_1_out_24), .in_7(n8_bit_adder_nd_1_out_25),
    .in_8(n8_bit_adder_nd_1_out_26));  // open: out_12, out_13, out_14, out_15, out_16, out_17, out_18, out_19
  _8_Bit_Register_Clock u_8_bit_register_clock_1 (
    .in_10(clock_1_out), .out_12(n8_bit_register_clock_1_out_12), .out_13(n8_bit_register_clock_1_out_13),
    .out_14(n8_bit_register_clock_1_out_14), .out_15(n8_bit_register_clock_1_out_15),
    .out_16(n8_bit_register_clock_1_out_16), .out_17(n8_bit_register_clock_1_out_17),
    .out_18(n8_bit_register_clock_1_out_18), .out_19(n8_bit_register_clock_1_out_19));  // open: in_9, in_11, in_1, in_2, in_3, in_4, in_5, in_6, in_7, in_8
  _8_Bit_Adder_ND u_8_bit_adder_nd_1 (
    .out_18(Cout), .in_17(1'b0), .in_1(Wert[7]), .in_2(Wert[6]), .in_3(Wert[5]), .in_4(Wert[4]),
    .in_5(Wert[3]), .in_6(Wert[2]), .in_7(Wert[1]), .in_8(Wert[0]), .in_9(n8_bit_register_clock_1_out_12),
    .in_10(n8_bit_register_clock_1_out_13), .in_11(n8_bit_register_clock_1_out_14),
    .in_12(n8_bit_register_clock_1_out_15), .in_13(n8_bit_register_clock_1_out_16),
    .in_14(n8_bit_register_clock_1_out_17), .in_15(n8_bit_register_clock_1_out_18),
    .in_16(n8_bit_register_clock_1_out_19), .out_19(n8_bit_adder_nd_1_out_19),
    .out_20(n8_bit_adder_nd_1_out_20), .out_21(n8_bit_adder_nd_1_out_21), .out_22(n8_bit_adder_nd_1_out_22),
    .out_23(n8_bit_adder_nd_1_out_23), .out_24(n8_bit_adder_nd_1_out_24), .out_25(n8_bit_adder_nd_1_out_25),
    .out_26(n8_bit_adder_nd_1_out_26));
endmodule

module Cycler (
  input  in_1,
  input  Reset,
  output out_3,
  output out_4,
  output out_5,
  output out_6,
  output out_7
);

  wire not_1_out, not_2_out, not_3_out, not_4_out, not_5_out;
  wire [7:0] counter_1_q;

  Counter_part #(.max('h4)) counter_1 (.Q(counter_1_q), .clk(in_1), .clr(Reset));  // open: load, D, count, carry
  nor nor_1 (out_3, counter_1_q[0], counter_1_q[1], counter_1_q[2]);
  not not_1 (not_1_out, counter_1_q[0]);
  nor nor_2 (out_4, not_1_out, counter_1_q[1], counter_1_q[2]);
  not not_2 (not_2_out, counter_1_q[1]);
  nor nor_3 (out_5, counter_1_q[0], not_2_out, counter_1_q[2]);
  not not_3 (not_3_out, counter_1_q[0]);
  nor nor_4 (out_6, not_3_out, not_4_out, counter_1_q[2]);
  not not_4 (not_4_out, counter_1_q[1]);
  nor nor_5 (out_7, counter_1_q[0], counter_1_q[1], not_5_out);
  not not_5 (not_5_out, counter_1_q[2]);
endmodule

module Index_Register (
  input  Increase,
  input  Reset,
  input  Read,
  input  clock,
  output [7:0] out_5
);

  wire or_1_out, or_2_out;
  wire [7:0] counter_1_q;

  Counter_part #(.ongoal("stay")) counter_1 (
    .Q(counter_1_q), .clk(Increase), .clr(Reset));  // open: load, D, count, carry
  or or_1 (or_1_out, Read, Reset, Increase);
  or or_2 (or_2_out, Reset, Increase);
  _8_Bit_Register_Clock Index (
    .in_9(or_1_out), .in_10(clock), .in_11(or_2_out), .in_1(counter_1_q[7]), .in_2(counter_1_q[6]),
    .in_3(counter_1_q[5]), .in_4(counter_1_q[4]), .in_5(counter_1_q[3]), .in_6(counter_1_q[2]),
    .in_7(counter_1_q[1]), .in_8(counter_1_q[0]), .out_12(out_5[7]), .out_13(out_5[6]), .out_14(out_5[5]),
    .out_15(out_5[4]), .out_16(out_5[3]), .out_17(out_5[2]), .out_18(out_5[1]), .out_19(out_5[0]));
endmodule

module _8_Bit_Decoder (
  input  in_1,
  input  in_2,
  input  in_3,
  input  in_4,
  input  in_5,
  input  in_6,
  input  in_7,
  input  in_8,
  output SUB,
  output ADD,
  output OR,
  output AND,
  output MOV,
  output LD,
  output HLT
);

  wire not_1_out, not_2_out, not_3_out, not_4_out, not_5_out, not_6_out, not_7_out, not_8_out, not_9_out;

  not not_1 (not_1_out, in_8);
  not not_2 (not_2_out, in_7);
  not not_3 (not_3_out, in_8);
  not not_4 (not_4_out, in_7);
  not not_5 (not_5_out, in_6);
  not not_6 (not_6_out, in_8);
  not not_7 (not_7_out, in_6);
  not not_8 (not_8_out, in_7);
  not not_9 (not_9_out, in_6);
  nor SUB_N (SUB, in_8, in_7, in_6, in_5, in_4);
  nor nor_1 (ADD, not_1_out, in_7, in_6, in_5, in_4);
  nor nor_2 (OR, in_8, not_2_out, in_6, in_5, in_4);
  nor nor_3 (AND, not_3_out, not_4_out, in_6, in_5, in_4);
  nor SUB_N_2 (MOV, in_8, in_7, not_5_out, in_5, in_4);
  nor SUB_N_3 (LD, not_6_out, in_7, not_7_out, in_5, in_4);
  nor SUB_N_4 (HLT, in_8, not_8_out, not_9_out, in_5, in_4);
endmodule

module is_ax (
  input  in_1,
  input  in_2,
  input  in_3,
  input  in_4,
  input  in_5,
  input  in_6,
  input  in_7,
  input  in_8,
  output out_9
);

  wire not_1_out;

  not not_1 (not_1_out, in_8);
  and and_1 (out_9, not_1_out, in_7, in_6, in_5, in_4, in_3, in_2);
endmodule

module is_bx (
  input  in_1,
  input  in_2,
  input  in_3,
  input  in_4,
  input  in_5,
  input  in_6,
  input  in_7,
  input  in_8,
  output out_9
);

  and and_1 (out_9, in_8, in_7, in_6, in_5, in_4, in_3, in_2);
endmodule
