// Logisim project speicherzelle.circ as structural Verilog: 1 circuit, main circuit main
module main (
  input  Select,
  input  in_2,
  input  in_3
);

  wire and_1_out, and_2_out, and_3_out, not_1_out, not_2_out, not_3_out, or_1_out, or_2_out;

  and and_1 (and_1_out, Select, in_2, in_3);
  not not_1 (not_1_out, in_2);
  and and_2 (and_2_out, Select, not_1_out, in_3);
  or or_1 (or_1_out, and_1_out, not_3_out);
  or or_2 (or_2_out, not_2_out, and_2_out);
  not not_2 (not_2_out, or_1_out);
  not not_3 (not_3_out, or_2_out);
  and and_3 (and_3_out, Select, not_3_out);

  // Notes on the sheet:
  //   set q = 1
  //   reset: q=0
  //   q
  //   Output
endmodule
