// Logisim project subtract_and_add.circ as structural Verilog: 2 circuits, main circuit main
module main (
  input  in_1,
  input  in_2,
  input  in_3,
  input  in_4,
  input  Add_sub,
  input  in_6,
  input  in_7,
  input  in_8,
  input  in_9
);

  wire and_1_out, and_2_out, and_3_out, and_4_out, and_5_out, and_6_out, and_7_out, and_8_out, or_1_out,
       or_2_out, or_3_out, or_4_out, xor_1_out, xor_2_out, xor_3_out, xor_4_out, xor_5_out, xor_6_out,
       xor_7_out, xor_8_out, xor_9_out, xor_10_out, xor_11_out, xor_12_out;

  LED led_1 (.in(or_1_out));
  and and_1 (and_1_out, xor_1_out, in_6);
  or or_1 (or_1_out, and_1_out, and_2_out);
  xor xor_1 (xor_1_out, in_1, Add_sub);
  xor xor_2 (xor_2_out, xor_1_out, in_6);
  and and_2 (and_2_out, xor_2_out, or_2_out);
  xor xor_3 (xor_3_out, xor_2_out, or_2_out);
  LED led_2 (.in(xor_3_out));
  or or_2 (or_2_out, and_3_out, and_4_out);
  xor xor_4 (xor_4_out, in_2, Add_sub);
  and and_3 (and_3_out, xor_4_out, in_7);
  xor xor_5 (xor_5_out, xor_4_out, in_7);
  and and_4 (and_4_out, xor_5_out, or_3_out);
  xor xor_6 (xor_6_out, xor_5_out, or_3_out);
  LED led_3 (.in(xor_6_out));
  and and_5 (and_5_out, xor_7_out, in_8);
  or or_3 (or_3_out, and_5_out, and_6_out);
  and and_6 (and_6_out, xor_8_out, or_4_out);
  xor xor_7 (xor_7_out, in_3, Add_sub);
  xor xor_8 (xor_8_out, xor_7_out, in_8);
  xor xor_9 (xor_9_out, xor_8_out, or_4_out);
  LED led_4 (.in(xor_9_out));
  and and_7 (and_7_out, xor_10_out, in_9);
  or or_4 (or_4_out, and_7_out, and_8_out);
  and and_8 (and_8_out, xor_11_out, Add_sub);
  xor xor_10 (xor_10_out, in_4, Add_sub);
  xor xor_11 (xor_11_out, xor_10_out, in_9);
  xor xor_12 (xor_12_out, xor_11_out, Add_sub);
  LED led_5 (.in(xor_12_out));
endmodule

module Adder_substracter (
  input  in_1,
  input  in_2,
  input  in_3,
  input  in_4,
  input  in_5,
  input  in_6,
  input  in_7,
  input  in_8
);

  wire and_1_out, and_2_out, and_3_out, and_4_out, and_5_out, and_6_out, and_7_out, and_8_out, or_1_out,
       or_2_out, or_3_out, or_4_out, undriven, undriven_2, xor_1_out, xor_2_out, xor_3_out, xor_4_out,
       xor_5_out, xor_6_out, xor_7_out, xor_8_out, xor_9_out, xor_10_out, xor_11_out, xor_12_out;

  and and_1 (and_1_out, xor_1_out, in_5);
  or or_1 (or_1_out, and_1_out, and_2_out);
  xor xor_1 (xor_1_out, in_1, undriven);
  xor xor_2 (xor_2_out, xor_1_out, in_5);
  and and_2 (and_2_out, xor_2_out, or_2_out);
  xor xor_3 (xor_3_out, xor_2_out, or_2_out);
  or or_2 (or_2_out, and_3_out, and_4_out);
  xor xor_4 (xor_4_out, in_2, undriven);
  and and_3 (and_3_out, xor_4_out, in_6);
  xor xor_5 (xor_5_out, xor_4_out, in_6);
  and and_4 (and_4_out, xor_5_out, or_3_out);
  xor xor_6 (xor_6_out, xor_5_out, or_3_out);
  and and_5 (and_5_out, xor_7_out, in_7);
  or or_3 (or_3_out, and_5_out, and_6_out);
  and and_6 (and_6_out, xor_8_out, or_4_out);
  xor xor_7 (xor_7_out, in_3, undriven);
  xor xor_8 (xor_8_out, xor_7_out, in_7);
  xor xor_9 (xor_9_out, xor_8_out, or_4_out);
  and and_7 (and_7_out, xor_10_out, in_8);
  or or_4 (or_4_out, and_7_out, and_8_out);
  and and_8 (and_8_out, xor_11_out, undriven_2);
  xor xor_10 (xor_10_out, in_4, undriven);
  xor xor_11 (xor_11_out, xor_10_out, in_8);
  xor xor_12 (xor_12_out, xor_11_out, undriven_2);
endmodule
