// Logisim project timed_rsflipflop.circ as structural Verilog: 1 circuit, main circuit main
module main (
  input  Select,
  input  Input,
  input  Write
);

  wire and_1_out, and_2_out, and_3_out, and_4_out, and_5_out, clock_1_out, not_1_out, not_2_out, not_3_out,
       not_4_out, not_5_out, not_6_out, not_7_out, or_1_out, or_2_out;

  Clock clock_1 (.out(clock_1_out));
  not not_1 (not_1_out, clock_1_out);
  not not_2 (not_2_out, not_1_out);
  and and_1 (and_1_out, clock_1_out, not_4_out);
  not not_3 (not_3_out, not_2_out);
  not not_4 (not_4_out, not_3_out);
  and and_2 (and_2_out, and_1_out, Select);
  and and_3 (and_3_out, and_2_out, Input, Write);
  not not_5 (not_5_out, Input);
  and and_4 (and_4_out, and_2_out, not_5_out, Write);
  or or_1 (or_1_out, and_3_out, not_7_out);
  or or_2 (or_2_out, and_4_out, not_6_out);
  not not_6 (not_6_out, or_1_out);
  not not_7 (not_7_out, or_2_out);
  and and_5 (and_5_out, and_2_out, not_6_out);
endmodule
